# Fritzing sketch konashiMotorDriveShield (saved by Fritzing 0.7.12b)
perfboards: 1

parts:
  J1 = female pin header, 10 pins [form="♀ (female)"]
  U1 = TA7291P [package=HSIP10-P-2.54(THT)]
  U2 = TA7291P [package=HSIP10-P-2.54(THT)]
  R2_(10k) = Resistor [tolerance=±5% resistance=10k package=THT]
  R1_(10k) = Resistor [tolerance=±5% resistance=10k power=0pW package=THT]
  J2 = female pin header, 10 pins [form="♀ (female)"]

nets:
  GND: J1.pin4, J1.pin10, U1.GND, U2.GND, J2.pin10
  PIO6: J1.pin5, U1.IN2
  PIO7: J1.pin6, U1.IN1
  N1: U1.Vref, R1_(10k).Pin_0
  +6V: U1.Vcc, U1.Vs, U2.Vcc, U2.Vs, R2_(10k).Pin_1, R1_(10k).Pin_1
  N2: U2.Vref, R2_(10k).Pin_0
  PIO5: U2.IN1, J2.pin9
  PIO4: U2.IN2, J2.pin8

notes:
  GND
  To Motor
  To V source
  MOTOR1
  MOTOR2
  To Motor1
  To Motor2

custom parts:
  TA7291P: The IC are Full-Bridge Driver. 4 modes available (CW / CCW / STOP / BRAKE) and PWM control. Output current:1.0 A (AVE.) 2.0 A (PEAK)
